// Digital circuit Contador.dig as structural Verilog
module Contador (
  input  R,
  input  CE,
  input  clk,
  input  D4,
  input  D3,
  input  D2,
  input  D1,
  input  L,
  output rout,
  output Q1,
  output Q2,
  output Q3,
  output Q4
);

  wire and_1_out, and_2_out, and_3_out, and_4_out, and_5_out, and_6_out, and_7_out, and_8_out,
       d_flipflop_rising_1_p2, half_adder_1_p1, half_adder_1_p3, half_adder_1_p5, half_adder_2_p1,
       half_adder_2_p3, half_adder_3_p1, half_adder_3_p3, not_1_out, or_1_out, or_2_out, or_3_out, or_4_out,
       plus_1_p10, plus_1_p12, plus_1_p13, plus_1_p14;

  not not_1 (not_1_out, L);
  // D_flipflop_rising d_flipflop_rising_1: pin names not known; wires that end beside it: clk, d_flipflop_rising_1_p2, R, rout
  // Half_Adder half_adder_1: pin names not known; wires that end beside it: half_adder_1_p1, d_flipflop_rising_1_p2, half_adder_1_p3, Q4, half_adder_1_p5, half_adder_1_p3
  // Half_Adder half_adder_2: pin names not known; wires that end beside it: half_adder_2_p1, Q3, half_adder_2_p3, half_adder_2_p1
  // Half_Adder half_adder_3: pin names not known; wires that end beside it: half_adder_3_p1, Q2, half_adder_3_p3, half_adder_3_p1
  and and_1 (and_1_out, not_1_out, half_adder_1_p1);
  and and_2 (and_2_out, not_1_out, half_adder_1_p5);
  and and_3 (and_3_out, not_1_out, half_adder_2_p3);
  and and_4 (and_4_out, not_1_out, half_adder_3_p3);
  or or_1 (or_1_out, L, CE);
  // Half_Adder half_adder_4: pin names not known; wires that end beside it: 1'b1, Q1
  or or_2 (or_2_out, and_8_out, and_1_out);
  or or_3 (or_3_out, and_6_out, and_3_out);
  or or_4 (or_4_out, and_7_out, and_2_out);
  // _4_Bit_Register plus_1: pin names not known; wires that end beside it: or_1_out, clk, R, or_2_out, Q4, or_4_out, Q3, or_3_out, Q2, plus_1_p10, Q1, plus_1_p12, plus_1_p13, plus_1_p14
  or or_5 (plus_1_p10, and_5_out, and_4_out);
  and and_5 (and_5_out, D1, L);
  and and_6 (and_6_out, D2, L);
  and and_7 (and_7_out, D3, L);
  and and_8 (and_8_out, D4, L);
  PullDown pulldown_1 ();  // open: out
  PullDown pulldown_2 (.out(plus_1_p12));
  PullDown pulldown_3 (.out(plus_1_p13));
  PullDown pulldown_4 (.out(plus_1_p14));

  // Notes on the sheet:
  //   CE: Loads D into internal register
endmodule
