// Digital circuit Decodificador.dig as structural Verilog
module Decodificador (
  input  D4,
  input  D3,
  input  D2,
  input  D1,
  output _0,
  output _1,
  output _2,
  output _3,
  output _4,
  output _5,
  output _6,
  output _7,
  output _8,
  output _9,
  output _10,
  output _11,
  output _12,
  output _13,
  output _14,
  output _15
);

  wire delay_1_out, delay_2_out, delay_3_out, delay_4_out, not_1_out, not_2_out, not_3_out, not_4_out;

  Delay delay_1 (.in(D4), .out(delay_1_out));
  not not_1 (not_1_out, D4);
  Delay delay_2 (.in(D3), .out(delay_2_out));
  not not_2 (not_2_out, D3);
  Delay delay_3 (.in(D2), .out(delay_3_out));
  not not_3 (not_3_out, D2);
  Delay delay_4 (.in(D1), .out(delay_4_out));
  not not_4 (not_4_out, D1);
  and and_1 (_0, not_1_out, not_2_out, not_3_out, not_4_out);
  and and_2 (_1, not_1_out, not_2_out, not_3_out, delay_4_out);
  and and_3 (_2, not_1_out, not_2_out, delay_3_out, not_4_out);
  and and_4 (_3, not_1_out, not_2_out, delay_3_out, delay_4_out);
  and and_5 (_4, not_1_out, delay_2_out, not_3_out, not_4_out);
  and and_6 (_5, not_1_out, delay_2_out, not_3_out, delay_4_out);
  and and_7 (_6, not_1_out, delay_2_out, delay_3_out, not_4_out);
  and and_8 (_7, not_1_out, delay_2_out, delay_3_out, delay_4_out);
  and and_9 (_8, delay_1_out, not_2_out, not_3_out, not_4_out);
  and and_10 (_9, delay_1_out, not_2_out, not_3_out, delay_4_out);
  and and_11 (_10, delay_1_out, not_2_out, delay_3_out, not_4_out);
  and and_12 (_11, delay_1_out, not_2_out, delay_3_out, delay_4_out);
  and and_13 (_12, delay_1_out, delay_2_out, not_3_out, not_4_out);
  and and_14 (_13, delay_1_out, delay_2_out, not_3_out, delay_4_out);
  and and_15 (_14, delay_1_out, delay_2_out, delay_3_out, not_4_out);
  and and_16 (_15, delay_1_out, delay_2_out, delay_3_out, delay_4_out);
endmodule
