// Digital circuit Registrador.dig as structural Verilog
module Registrador (
  input  load,
  input  D4,
  input  c,
  input  R,
  input  D3,
  input  D2,
  input  D1,
  output Q4,
  output Q3,
  output Q2,
  output Q1
);

  wire pullup_1_out, pullup_2_out, pullup_3_out, pullup_4_out;

  PullUp pullup_1 (.out(pullup_1_out));
  PullUp pullup_2 (.out(pullup_2_out));
  PullUp pullup_3 (.out(pullup_3_out));
  PullUp pullup_4 (.out(pullup_4_out));
  // Bit bit_1: pin names not known; wires that end beside it: pullup_1_out, load, 1'b1, D1, c, R, Q1
  // Bit bit_2: pin names not known; wires that end beside it: pullup_2_out, pullup_3_out, load, 1'b1, D2, c, R, Q2
  // Bit bit_3: pin names not known; wires that end beside it: pullup_4_out, load, 1'b1, D3, c, R, Q3
  // Bit bit_4: pin names not known; wires that end beside it: load, 1'b1, D4, c, R, Q4

  // Notes on the sheet:
  //   load: pin 5
  //   D4: pin 4
  //   c: pin 7
  //   R: pin 8
  //   D3: pin 3
  //   D2: pin 2
  //   D1: pin 1
endmodule
